# Fritzing sketch LCD UNO&ETC (saved by Fritzing 0.9.3b)
breadboards: 1

parts:
  LCD1 = LCD screen
  R1 = Rotary Potentiometer (Large) [maximum_resistance=100kΩ package=THT]
  Composant1 = Arduino Leonardo (Rev3b)

nets:
  VSS: LCD1.VSS, LCD1.R/W, LCD1.LED-, R1.leg2, Composant1.GND
  VDD: LCD1.VDD, LCD1.LED+, R1.leg1, Composant1.5V
  N1: LCD1.V0, R1.wiper
  N2: LCD1.RS, Composant1.D12/A11
  N3: LCD1.E, Composant1.D11_PWM
  N4: LCD1.DB4, Composant1.D5_PWM
  N5: LCD1.DB5, Composant1.D4/A6
  N6: LCD1.DB6, Composant1.D3_PWM/SCL
  N7: LCD1.DB7, Composant1.D2/SDA
